# Fritzing sketch gibbon-v1128 (saved by Fritzing 0.9.2b)

parts:
  mega = Arduino Mega 2560 (Rev3)  # not connected
  mega_shield = Arduino Mega Proto Shield (v6)
  IC1 = H-Bridge [package=THT]
  IC2 = H-Bridge [package=THT]
  IC3 = H-Bridge [package=THT]
  Fan1 = DC Motor
  Fan2 = DC Motor
  Fan3 = DC Motor
  Fan4 = DC Motor
  Fan5 = DC Motor
  Fan6 = DC Motor
  Bubble1 = Basic Servo  # not connected
  Bubble2 = Basic Servo  # not connected
  Bubble3 = Basic Servo  # not connected
  Bubble4 = Basic Servo  # not connected
  Bubble5 = Basic Servo  # not connected
  Bubble6 = Basic Servo  # not connected
  Servo2L = Basic Servo  # not connected
  Servo3R = Basic Servo  # not connected
  Servo3L = Basic Servo  # not connected
  Servo2R = Basic Servo  # not connected
  Servo1L = Basic Servo  # not connected
  Servo1R = Basic Servo  # not connected
  Servo5L = Basic Servo  # not connected
  Servo6R = Basic Servo  # not connected
  Servo6L = Basic Servo  # not connected
  Servo5R = Basic Servo  # not connected
  Servo4L = Basic Servo  # not connected
  Servo4R = Basic Servo  # not connected
  J1 = male pin header, 12 pins [form="♂ (male)"]

nets:
  N1: mega_shield.N$58, IC3.1A
  N2: mega_shield.N$59, IC3.1_2EN
  N3: mega_shield.N$94, IC3.4A
  N4: mega_shield.N$95, IC3.VCC1
  N5: mega_shield.N$153, IC2.GND2
  N6: mega_shield.N$155, IC1.1A
  N7: mega_shield.N$156, IC1.1_2EN
  N8: mega_shield.N$189, IC2.3_4EN
  N9: mega_shield.N$191, IC1.4A
  N10: mega_shield.N$192, IC1.VCC1
  N11: mega_shield.N$231, IC1.1Y
  N12: mega_shield.N$232, IC1.GND1
  N13: mega_shield.N$234, IC1.GND2
  N14: mega_shield.N$237, IC1.2Y
  N15: mega_shield.N$240, IC1.2A
  N16: mega_shield.N$245, IC1.GND4
  N17: mega_shield.N$246, IC1.GND3
  N18: mega_shield.N$247, mega_shield.N$437, IC1.4Y
  N19: mega_shield.N$273, IC3.4Y
  N20: mega_shield.N$281, IC3.3Y
  N21: mega_shield.N$282, IC3.3A
  N22: mega_shield.N$284, IC3.1Y
  N23: mega_shield.N$285, IC3.GND1
  N24: mega_shield.N$291, IC3.GND2
  N25: mega_shield.N$292, IC3.2Y
  N26: mega_shield.N$295, IC3.3_4EN
  N27: mega_shield.N$307, IC2.1_2EN
  N28: mega_shield.N$308, Fan5.pin_2, J1.pin3
  N29: mega_shield.N$309, IC2.1Y
  N30: mega_shield.N$310, IC2.1A
  N31: mega_shield.N$311, IC1.VCC2
  N32: mega_shield.N$314, IC3.GND4
  N33: mega_shield.N$315, IC3.GND3
  N34: mega_shield.N$328, Fan2.pin_2, J1.pin9
  N35: mega_shield.N$330, Fan3.pin_1, J1.pin8
  N36: mega_shield.N$333, Fan3.pin_2, J1.pin7
  N37: mega_shield.N$334, Fan4.pin_1, J1.pin6
  N38: mega_shield.N$337, Fan4.pin_2, J1.pin5
  N39: mega_shield.N$340, Fan5.pin_1, J1.pin4
  N40: mega_shield.N$342, Fan1.pin_1, J1.pin12
  N41: mega_shield.N$343, Fan1.pin_2, J1.pin11
  N42: mega_shield.N$344, Fan2.pin_1, J1.pin10
  N43: mega_shield.N$362, IC3.VCC2
  N44: mega_shield.N$363, IC3.2A
  N45: mega_shield.N$398, IC2.2A
  N46: mega_shield.N$399, IC2.2Y
  N47: mega_shield.N$400, IC2.GND1
  N48: mega_shield.N$416, IC1.3Y
  N49: mega_shield.N$417, IC1.3_4EN
  N50: mega_shield.N$418, IC1.3A
  N51: mega_shield.N$419, IC2.VCC1
  N52: mega_shield.N$420, IC2.4A
  N53: mega_shield.N$421, IC2.4Y
  N54: mega_shield.N$422, IC2.GND4
  N55: mega_shield.N$423, IC2.GND3
  N56: mega_shield.N$424, IC2.3Y
  N57: mega_shield.N$425, IC2.3A
  N58: mega_shield.N$446, Fan6.pin_1, J1.pin2
  N59: mega_shield.N$457, Fan6.pin_2, J1.pin1
  N60: mega_shield.N$460, IC2.VCC2

notes:
  DCmotor(fan)
  1 +
  2 -
  3
  4
  5
  5
  6
  7
  8
  9
  10
  11
  12s
